// Logisim project GATES.circ as structural Verilog: 1 circuit, main circuit main
module main (
  input  NAND,
  input  in_2,
  input  in_3,
  input  NOR,
  input  in_5,
  input  in_6,
  input  in_7,
  input  in_8,
  input  in_9,
  input  XOR,
  input  in_11,
  output out_12,
  output out_13,
  output out_14,
  output out_15,
  output out_16,
  output out_17
);

  wire transistor_3_out, transistor_9_out, transistor_13_out, transistor_14_out, transistor_18_out,
       transistor_20_out, transistor_21_out;

  Transistor transistor_1 (.in(1'b1), .out(out_12), .gate(in_5));
  Transistor #(.\type ("n")) transistor_2 (.in(1'b0), .out(out_12), .gate(in_5));
  Transistor #(.\type ("n")) transistor_3 (.in(1'b1), .out(transistor_3_out), .gate(in_3));
  Transistor #(.\type ("n")) transistor_4 (.in(transistor_3_out), .out(out_15), .gate(in_6));
  Transistor transistor_5 (.in(1'b0), .out(out_15), .gate(in_3));
  Transistor transistor_6 (.in(1'b0), .out(out_15), .gate(in_6));
  Transistor transistor_7 (.in(1'b1), .out(out_13), .gate(NAND));
  Transistor #(.\type ("n")) transistor_8 (.in(transistor_9_out), .out(out_13), .gate(NAND));
  Transistor #(.\type ("n")) transistor_9 (.in(1'b0), .out(transistor_9_out), .gate(in_8));
  Transistor transistor_10 (.in(1'b1), .out(out_13), .gate(in_8));
  Transistor #(.\type ("n")) transistor_11 (.in(1'b1), .out(out_14), .gate(in_2));
  Transistor transistor_12 (.in(transistor_13_out), .out(out_14), .gate(in_2));
  Transistor transistor_13 (.in(1'b0), .out(transistor_13_out), .gate(in_9));
  Transistor transistor_14 (.in(1'b1), .out(transistor_14_out), .gate(XOR));
  Transistor #(.\type ("n")) transistor_15 (.in(1'b1), .out(out_14), .gate(in_9));
  Transistor transistor_16 (.in(1'b1), .out(transistor_14_out), .gate(in_11));
  Transistor #(.\type ("n")) transistor_17 (.in(transistor_18_out), .out(transistor_14_out), .gate(XOR));
  Transistor #(.\type ("n")) transistor_18 (.in(transistor_20_out), .out(transistor_18_out), .gate(in_11));
  Transistor transistor_19 (.in(1'b1), .out(out_17), .gate(transistor_14_out));
  Transistor #(.\type ("n")) transistor_20 (.in(out_17), .out(transistor_20_out), .gate(transistor_14_out));
  Transistor transistor_21 (.in(1'b1), .out(transistor_21_out), .gate(NOR));
  Transistor transistor_22 (.in(transistor_21_out), .out(out_16), .gate(in_7));
  Transistor #(.\type ("n")) transistor_23 (.in(1'b0), .out(out_16), .gate(NOR));
  Transistor #(.\type ("n")) transistor_24 (.in(1'b0), .out(out_16), .gate(in_7));
  Controlled_Inverter controlled_inverter_1 ();  // open: in, out, en
  // also tied to GND on the sheet: transistor_20_out

  // Notes on the sheet:
  //   Invertor
  //   AND
  //   NAND
  //   OR
endmodule
