// Logisim project MUX.circ as structural Verilog: 2 circuits, main circuit main
module main (
  input  B,
  input  s,
  input  A,
  output out_4
);

  wire nand_1_out, nand_2_out, nand_3_out;

  nand nand_1 (nand_1_out, s, s);
  nand nand_2 (nand_2_out, B, s);
  nand nand_3 (nand_3_out, nand_1_out, A);
  nand nand_4 (out_4, nand_2_out, nand_3_out);
endmodule

module Mux (
  input  _1,
  input  _2,
  input  _3,
  input  _4,
  input  [1:0] in_5,
  output out_6
);

  wire main_1_out_4, main_2_out_4;

  main main_1 (.B(_2), .s(in_5[0]), .A(_1), .out_4(main_1_out_4));
  main main_2 (.B(_4), .s(in_5[0]), .A(_3), .out_4(main_2_out_4));
  // Probe on main_1_out_4
  // Probe on main_2_out_4
  main main_3 (.B(main_2_out_4), .s(in_5[1]), .A(main_1_out_4), .out_4(out_6));
endmodule
