// Logisim project adder.circ as structural Verilog: 1 circuit, main circuit main
module main (
  input  A,
  input  B,
  output C_out,
  output Sum,
  output Sum_2,
  output Count
);

  wire and_2_out, and_3_out, xor_1_out;

  xor xor_1 (xor_1_out, A, B);
  and and_1 (C_out, A, B);
  xor xor_2 (Sum, A, B);
  xor xor_3 (Sum_2, xor_1_out, C_out);
  and and_2 (and_2_out, C_out, xor_1_out);
  and and_3 (and_3_out, A, B);
  or or_1 (Count, and_2_out, and_3_out);

  // Notes on the sheet:
  //   Cin
  //   Half adder
  //   Full Adder
endmodule
