// Logisim project comparator.circ as structural Verilog: 2 circuits, main circuit main
module main (
  input  A,
  input  B,
  output out_3,
  output out_4,
  output out_5
);

  wire not_1_out, not_2_out;

  not not_1 (not_1_out, A);
  not not_2 (not_2_out, B);
  and and_1 (out_3, A, not_2_out);
  xnor xnor_1 (out_4, A, B);
  and and_2 (out_5, not_1_out, B);
endmodule

module _1bit_comparator (
);

  main main_1 ();  // open: A, B, out_3, out_4, out_5
  main main_2 ();  // open: A, B, out_3, out_4, out_5
endmodule
