// Logisim project flipflop.circ as structural Verilog: 2 circuits, main circuit main
module main (
  input  D,
  input  CLK,
  output out_3,
  output out_4
);

  wire nand_1_out, nand_2_out, not_1_out;

  not not_1 (not_1_out, CLK);
  nand nand_1 (nand_1_out, D, not_1_out);
  nand nand_2 (nand_2_out, nand_1_out, not_1_out);
  nand nand_3 (out_3, nand_1_out, out_4);
  nand nand_4 (out_4, out_3, nand_2_out);
endmodule

module D_flip_flop (
  input  in_1,
  input  in_2,
  input  in_3,
  output out_4,
  output out_5,
  output out_6
);

  wire clock_1_out, clock_2_out, clock_3_out, d_ff_1_q, d_ff_2_q, d_ff_3_q, main_1_out_3, main_2_out_3,
       main_3_out_3, main_4_out_3, main_5_out_3, main_6_out_3;

  Clock clock_1 (.out(clock_1_out));
  Clock clock_2 (.out(clock_2_out));
  main main_1 (.D(in_2), .CLK(clock_1_out), .out_3(main_1_out_3));  // open: out_4
  main main_2 (.D(in_3), .CLK(clock_2_out), .out_3(main_2_out_3));  // open: out_4
  main main_3 (.D(main_1_out_3), .CLK(clock_1_out), .out_3(main_3_out_3));  // open: out_4
  main main_4 (.D(main_2_out_3), .CLK(clock_2_out), .out_3(main_4_out_3));  // open: out_4
  main main_5 (.D(main_3_out_3), .CLK(clock_1_out), .out_3(main_5_out_3));  // open: out_4
  main main_6 (.D(main_4_out_3), .CLK(clock_2_out), .out_3(main_6_out_3));  // open: out_4
  main main_7 (.D(main_5_out_3), .CLK(clock_1_out), .out_3(out_5));  // open: out_4
  main main_8 (.D(main_6_out_3), .CLK(clock_2_out), .out_3(out_6));  // open: out_4
  Clock clock_3 (.out(clock_3_out));
  D_Flip_Flop d_ff_1 (.clk(clock_3_out), .D(in_1), .Q(d_ff_1_q));  // open: Qn, preset, en, reset
  D_Flip_Flop d_ff_2 (.clk(clock_3_out), .D(d_ff_1_q), .Q(d_ff_2_q));  // open: Qn, preset, en, reset
  D_Flip_Flop d_ff_3 (.clk(clock_3_out), .D(d_ff_2_q), .Q(d_ff_3_q));  // open: Qn, preset, en, reset
  D_Flip_Flop d_ff_4 (.clk(clock_3_out), .D(d_ff_3_q), .Qn(out_4));  // open: Q, preset, en, reset

  // Notes on the sheet:
  //   level trigerred
endmodule
